# Fritzing sketch Joystick Example (saved by Fritzing 0.9.3b)
circuit board: 5.76083cm x 3.46516cm
breadboards: 1

parts:
  Mod1 = Raspberry Pi Pico
  OLED_I2C1 = OLED 128x64 I2C Monochrome Display
  Componente1 = Thumb Joystick

nets:
  N1: Mod1.pin_3, Mod1.pin_8, Mod1.pin_13, Mod1.pin_18, Mod1.pin_23, Mod1.pin_28, Mod1.pin_33, Mod1.pin_38
  N2: Mod1.pin_24, OLED_I2C1.SDA
  N3: Mod1.pin_25, OLED_I2C1.SCK
  N4: Mod1.pin_31, Componente1.VERT
  N5: Mod1.pin_32, Componente1.HORZ
  N6: Mod1.pin_34, Componente1.SEL

custom parts:
  Raspberry Pi Pico: Raspberry Pi Pico. Based around the RP2040 microcontroller the Pico is a low cost microcontroller device bringing Raspberry Pi quality, cost, and easy of use to the microcontroller space. Jan 2021, Split part in to two versions: tht (this one) and SMD. This one will drill holes for a .1 in header in pcb to allow plugging in the module as well as providing pads to solder the module to the top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
